# Fritzing sketch Galvanico358 (saved by Fritzing 0.8.3b)
circuit board: 7.08378cm x 6.13833cm
breadboards: 1

parts:
  power = screw terminal, 2 pins
  electrodos = screw terminal, 2 pins
  lm358n = LM 358 Dual Op-Amp [package="DIP8 [THT]"]
  500K = Rotary Potentiometer (Small) [maximum_resistance=250]
  250K = Rotary Potentiometer (Small) [maximum_resistance=100kΩ]
  GND = female pin header, 1 pin [form="♀ (female)"]
  1K = Resistor [tolerance=±5% resistance=220 package=THT]
  3_3K = Resistor [tolerance=±5% resistance=220 package=THT]
  4_7K = Resistor [tolerance=±5% resistance=220 package=THT]
  1uF = Electrolytic Capacitor [capacitance=1µF package="100 mil [THT, electrolytic]"]
  1K_2 = Resistor [tolerance=±5% resistance=220 package=THT]
  3M = Resistor [tolerance=±5% resistance=220 package=THT]
  650K = Resistor [tolerance=±5% resistance=220 package=THT]
  750K = Resistor [tolerance=±5% resistance=220 package=THT]
  salida = female pin header, 1 pin [form="♀ (female)"]

nets:
  N1: power.pin1, electrodos.pin2, lm358n.connector3, 500K.leg1, GND.pin1, 1uF.-, 750K.Pin_1
  N2: power.pin2, lm358n.connector7, 500K.leg2, 3M.Pin_1, 650K.Pin_0
  N3: electrodos.pin1, 1K.Pin_1, 3M.Pin_0
  N4: lm358n.connector0, 3_3K.Pin_0, 4_7K.Pin_0
  N5: lm358n.connector1, 3_3K.Pin_1, 1K_2.Pin_0
  N6: lm358n.connector2, 1K.Pin_0
  N7: 250K.leg1, 650K.Pin_1
  N8: 250K.wiper, 1K_2.Pin_1
  N9: 250K.leg2, 750K.Pin_0
  N10: 4_7K.Pin_1, 1uF.+, salida.pin1

notes:
  Pulsu(m)
  Plantae
  bio-sensor
  http://lessnullvoid.cc/pulsum
  ∆
