# Fritzing sketch GalvanicoLM324n (saved by Fritzing 0.7.10b)
breadboards: 1

parts:
  U3 = SN74LS20N [package="DIP14 [THT]"]
  Part3 = Variable Capacitor [capacitance=100nF max_capacitance=10pF min_capacitance=2pF voltage=35V]
  Part4 = Variable Capacitor [capacitance=100nF max_capacitance=10pF min_capacitance=2pF voltage=35V]
  R9 = Resistor [tolerance=±5% resistance=100 package=THT]
  R10 = Resistor [tolerance=±5% resistance=220 package=THT]
  R11 = Resistor [tolerance=±5% resistance=220 package=THT]
  R12 = Resistor [tolerance=±5% resistance=100 package=THT]
  R13 = Resistor [tolerance=±5% resistance=220 package=THT]
  R14 = Resistor [tolerance=±5% resistance=220 package=THT]
  R15 = Resistor [tolerance=±5% resistance=100 package=THT]
  J9 = female pin header, 1 pin [form="♀ (female)"]
  J10 = female pin header, 2 pins [form="♀ (female)"]
  J7 = screw terminal, 2 pins
  J8 = screw terminal, 2 pins

nets:
  N1: U3.1A, R13.Pin_0, R15.Pin_0
  N2: U3.1B, Part4.2, R15.Pin_1
  N3: U3.NC#2, R10.Pin_0, J7.pin1
  N4: U3.1C, J8.pin1
  N5: U3.1D, J10.pin1, J7.pin2
  N6: U3.1Y, Part4.0, R12.Pin_0
  N7: U3.GND, R11.Pin_0, R12.Pin_1
  N8: U3.2Y, R9.Pin_1, J9.pin1
  N9: U3.2A, R9.Pin_0, R13.Pin_1
  N10: U3.2B, R11.Pin_1, R14.Pin_1
  N11: U3.NC#10, Part3.2, R14.Pin_0, J10.pin2, J8.pin2
  N12: Part3.1, R10.Pin_1

notes:
  lm324n
  Pulsu(m) Plantae
