# Fritzing sketch GalvanicoLM324n2 (saved by Fritzing 0.8.5b)
circuit board: 7.714cm x 5.3509cm
breadboards: 1

parts:
  LM324N = SN74LS20N [package="DIP14 [THT]"]
  100k = Variable Capacitor [capacitance=100nF max_capacitance=10pF min_capacitance=2pF voltage=35V]
  1M = Variable Capacitor [capacitance=100nF max_capacitance=10pF min_capacitance=2pF voltage=35V]
  100k_2 = Resistor [tolerance=±5% resistance=100 package=THT]
  1M_2 = Resistor [tolerance=±5% resistance=220 package=THT]
  10K = Resistor [tolerance=±5% resistance=220 package=THT]
  100k_3 = Resistor [tolerance=±5% resistance=100 package=THT]
  10K_2 = Resistor [tolerance=±5% resistance=10k package=THT]
  10k = Resistor [tolerance=±5% resistance=10k package=THT]
  100k_4 = Resistor [tolerance=±5% resistance=100 package=THT]
  salida = female pin header, 1 pin [form="♀ (female)"]
  1_5v = female pin header, 2 pins [form="♀ (female)"]
  electrodos = screw terminal, 2 pins
  power = screw terminal, 2 pins

nets:
  N1: LM324N.1A, 10K_2.Pin_0, 100k_4.Pin_0
  N2: LM324N.1B, 1M.2, 100k_4.Pin_1
  N3: LM324N.NC#2, 1M_2.Pin_0, electrodos.pin1
  N4: LM324N.1C, power.pin1
  N5: LM324N.1D, 1_5v.pin1, electrodos.pin2
  N6: LM324N.1Y, 1M.0, 100k_3.Pin_0
  N7: LM324N.GND, 10K.Pin_0, 100k_3.Pin_1
  N8: LM324N.2Y, 100k_2.Pin_1, salida.pin1
  N9: LM324N.2A, 100k_2.Pin_0, 10K_2.Pin_1
  N10: LM324N.2B, 10K.Pin_1, 10k.Pin_1
  N11: LM324N.NC#10, 100k.2, 10k.Pin_0, 1_5v.pin2, power.pin2
  N12: 100k.1, 1M_2.Pin_1

notes:
  galvanico
  http://lessnullvoid.cc/pulsum
  ∆
  bio-sensor
  Plantae
  Pulsu(m)
